# Fritzing sketch main (saved by Fritzing 0.9.2b)
breadboards: 1

parts:
  Raspberry_Pi_2 = Raspberry Pi 2
  Port3 = shrouded pin header, 6 pins [form="♂ (shrouded male)"]
  Port2 = shrouded pin header, 6 pins [form="♂ (shrouded male)"]
  Port1 = shrouded pin header, 6 pins [form="♂ (shrouded male)"]
  GPS = female pin header, 9 pins [form="♀ (female)"]
  M2 = male pin header, 2 pins [form="♂ (male)"]
  M3 = male pin header, 2 pins [form="♂ (male)"]
  M4 = male pin header, 2 pins [form="♂ (male)"]
  M1 = male pin header, 2 pins [form="♂ (male)"]
  A3 = male pin header, 3 pins [form="♂ (male)"]
  A2 = male pin header, 3 pins [form="♂ (male)"]
  A1 = male pin header, 3 pins [form="♂ (male)"]
  A0 = male pin header, 3 pins [form="♂ (male)"]
  J1 = female pin header, 2 pins [form="♀ (female)"]
  J2 = female pin header, 2 pins [form="♀ (female)"]
  Disp = male pin header, 3 pins [form="♂ (male)"]
  Port4 = shrouded pin header, 6 pins [form="♂ (shrouded male)"]
  U4 = SSOP20 [chip_label=74LVC244 package=SSOP]
  R5 = Resistor [tolerance=±1% resistance=10k package="0805 [SMD]"]
  R8 = Resistor [tolerance=±1% resistance=100k package="0805 [SMD]"]
  R13 = Resistor [tolerance=±1% resistance=10k package="0805 [SMD]"]
  R1 = Resistor [tolerance=±1% resistance=10k package="0805 [SMD]"]
  R4 = Resistor [tolerance=±1% resistance=10k package="0805 [SMD]"]
  R3 = Resistor [tolerance=±1% resistance=10k package="0805 [SMD]"]
  R2 = Resistor [tolerance=±1% resistance=10k package="0805 [SMD]"]
  C4 = Ceramic Capacitor [capacitance=100nF package="0805 [SMD, multilayer]"]
  C3 = Ceramic Capacitor [capacitance=100nF package="0805 [SMD, multilayer]"]
  C2 = Ceramic Capacitor [capacitance=22pF package="0805 [SMD, multilayer]"]
  C1 = Ceramic Capacitor [capacitance=22pF package="0805 [SMD, multilayer]"]
  Q2 = MOSFET-NCHANNEL [package=sot23-3]
  Q1 = MOSFET-NCHANNEL [package=sot23-3]
  Q4 = MOSFET-NCHANNEL [package=sot23-3]
  U3 = LT3514 [package=tssop-24]
  C5 = Ceramic Capacitor [capacitance=1µF package="0805 [SMD, multilayer]"]
  L1 = Inductor [inductance=10µH package="0805 [SMD]"]
  L2 = Inductor [inductance=4.7µH package="400 mil [THT]"]
  D1 = DIODE-SCHOTTKY [package=sma-diode]
  LED1 = Tri-Color LED SMD [package=led-tricolor-smd]  # not connected
  C11 = Ceramic Capacitor [capacitance=47pF package="0805 [SMD, multilayer]"]
  C6 = Ceramic Capacitor [capacitance=1µF package="0805 [SMD, multilayer]"]
  C7 = Ceramic Capacitor [capacitance=1µF package="0805 [SMD, multilayer]"]
  C10 = Ceramic Capacitor [capacitance=47nF package="0805 [SMD, multilayer]"]
  R14 = Resistor [tolerance=±1% resistance=18.2k package="1206 [SMD]"]
  R15 = Resistor [tolerance=±1% resistance=31.6k package="0805 [SMD]"]
  C12 = Ceramic Capacitor [capacitance=47µF package="0805 [SMD, multilayer]"]
  R16 = Resistor [tolerance=±1% resistance=10.2k package="0805 [SMD]"]
  D2 = DIODE-SCHOTTKY [package=sma-diode]
  L3 = Inductor [inductance=8.2µH package="400 mil [THT]"]
  C13 = Ceramic Capacitor [capacitance=22pF package="0805 [SMD, multilayer]"]
  R17 = Resistor [tolerance=±1% resistance=53.6k package="0805 [SMD]"]
  C14 = Ceramic Capacitor [capacitance=22µF package="0805 [SMD, multilayer]"]
  R18 = Resistor [tolerance=±1% resistance=10.2k package="0805 [SMD]"]
  D3 = DIODE-SCHOTTKY [package=sma-diode]
  L4 = Inductor [inductance=8.2µH package="400 mil [THT]"]
  C15 = Ceramic Capacitor [capacitance=22pF package="0805 [SMD, multilayer]"]
  R19 = Resistor [tolerance=±1% resistance=53.6k package="0805 [SMD]"]
  C16 = Ceramic Capacitor [capacitance=22µF package="0805 [SMD, multilayer]"]
  R20 = Resistor [tolerance=±1% resistance=10.2k package="0805 [SMD]"]
  PWR = male pin header, 4 pins [form="♂ (male)"]
  Q5 = MOSFET-NCHANNEL [package=sot23-3]
  Q6 = MOSFET-NCHANNEL [package=sot23-3]
  R9 = Resistor [tolerance=±1% resistance=100k package="0805 [SMD]"]
  R10 = Resistor [tolerance=±1% resistance=100k package="0805 [SMD]"]
  U2 = SOIC-14 [chip_label=ATTINY24 package=SO]
  C9 = Ceramic Capacitor [capacitance=47nF package="0805 [SMD, multilayer]"]
  C8 = Ceramic Capacitor [capacitance=47nF package="0805 [SMD, multilayer]"]
  C17 = Ceramic Capacitor [capacitance=100nF package="0805 [SMD, multilayer]"]
  R11 = Resistor [tolerance=±1% resistance=220 package="0805 [SMD]"]
  R12 = Resistor [tolerance=±1% resistance=220 package="0805 [SMD]"]
  R6 = Resistor [tolerance=±1% resistance=10k package="0805 [SMD]"]
  Q3 = MOSFET-NCHANNEL [package=sot23-3]
  R7 = Resistor [tolerance=±1% resistance=100k package="0805 [SMD]"]
  ISP2 = double row male pin header, 6 pins [form="♂ (male)"]
  ISP1 = double row male pin header, 6 pins [form="♂ (male)"]
  XTAL1 = CRYSTAL - kHz [frequency="16 Mhz"]
  U1 = ATmega328 [package=tqfp]
  L5 = Inductor [package="0805 [SMD]"]
  A6 = male pin header, 3 pins [form="♂ (male)"]
  A7 = male pin header, 3 pins [form="♂ (male)"]

nets:
  3.3V_SDA: Raspberry_Pi_2.GPIO2, R1.Pin_0, Q1.S
  3.3V_SCL: Raspberry_Pi_2.GPIO3, R2.Pin_0, Q2.S
  PI_MOSI: Raspberry_Pi_2.GPIO10, U4.6, U4.15
  PI_MISO: Raspberry_Pi_2.GPIO9, U4.3, U4.12
  PI_SCK: Raspberry_Pi_2.GPIO11, U4.4, U4.13
  GND: Raspberry_Pi_2.GND, Port3.pin3, Port3.pin6, Port2.pin3, Port2.pin6, Port1.pin3, Port1.pin6, GPS.pin7, A3.pin3, A2.pin3, A1.pin3, A0.pin3, Disp.pin3, Port4.pin3, Port4.pin6, U4.10, R8.Pin_0, C4.1, C3.1, C2.0, C1.0, Q4.S, U3.GND, C6.0, C7.0, C10.0, R14.Pin_0, C12.0, R16.Pin_1, C14.0, R18.Pin_1, C16.0, R20.Pin_1, PWR.pin4, Q5.S, Q6.S, R9.Pin_0, R10.Pin_0, U2.14, C9.0, C8.0, C17.1, R12.Pin_0, Q3.S, R7.Pin_0, ISP2.pin4, ISP1.pin4, U1.GND, A6.pin3, A7.pin3
  N1: Raspberry_Pi_2.GPIO26, GPS.pin2
  PI_CE1: Raspberry_Pi_2.GPIO7, U4.19, R6.Pin_1
  PI_CE0: Raspberry_Pi_2.GPIO8, U4.1, R5.Pin_0
  N2: Raspberry_Pi_2.GPIO15, GPS.pin5, J2.pin1
  N3: Raspberry_Pi_2.GPIO14, GPS.pin6, J1.pin1
  5V: Port3.pin1, Port2.pin1, Port1.pin1, A3.pin2, A2.pin2, A1.pin2, A0.pin2, Disp.pin2, Port4.pin1, R13.Pin_0, R4.Pin_1, R3.Pin_1, C3.0, L3.pin_1, C13.1, R17.Pin_1, C14.1, ISP1.pin6, U1.VCC, L5.pin_0, A6.pin2, A7.pin2
  3.3V: Port3.pin2, Port2.pin2, Port1.pin2, GPS.pin1, Port4.pin2, U4.20, R5.Pin_1, R1.Pin_1, R2.Pin_1, Q2.G, Q1.G, L2.pin_1, C11.1, R15.Pin_1, C12.1, R6.Pin_0
  5V_SDA: Port3.pin4, Port2.pin4, Port1.pin4, Port4.pin4, R4.Pin_0, Q1.D, PWR.pin1, U1.PC4(ADC4_SDA)
  5V_SCL: Port3.pin5, Port2.pin5, Port1.pin5, Port4.pin5, R3.Pin_0, Q2.D, PWR.pin2, U1.PC5(ADC5_SCL)
  AVR_D4: M2.pin1, U1.PD4(XCK_T0)
  PWM1: M2.pin2, U1.PD5(T1)
  AVR_D7: M3.pin1, U1.PD7(AIN1)
  PWM2: M3.pin2, U1.PD6(AIN0)
  AVR_D8: M4.pin1, U1.PB0(ICP)
  PWM3: M4.pin2, U1.PB1(OC1A)
  AVR_D2: M1.pin1, U1.PD2(INT0)
  PWM0: M1.pin2, U1.PD3(INT1)
  ADC3: A3.pin1, U1.PC3(ADC3)
  ADC2: A2.pin1, U1.PC2(ADC2)
  ADC1: A1.pin1, U1.PC1(ADC1)
  ADC0: A0.pin1, U1.PC0(ADC0)
  AVR_TX: J1.pin2, U1.PD1(TXD)
  AVR_RX: J2.pin2, U1.PD0(RXD)
  N4: Disp.pin1, U1.PB2(SS_OC1B)
  U2_MOSI: U4.5, U2.7, ISP2.pin5
  U2_SCK: U4.7, U2.9, ISP2.pin2
  U1_MISO: U4.8, ISP1.pin1, U1.PB4(MISO)
  N5: U4.9, Q3.G, R7.Pin_1
  U1_MOSI: U4.14, ISP1.pin5, U1.PB3(MOSI_OC2)
  U1_SCK: U4.16, ISP1.pin2, U1.PB5(SCK)
  U2_MISO: U4.17, U2.8, ISP2.pin1
  N6: U4.18, R8.Pin_1, Q4.G
  U1_RST: R13.Pin_1, Q4.D, ISP1.pin3, U1.PC6(_RESET)
  N7: C4.0, U1.AVCC, L5.pin_1
  N8: C2.1, XTAL1.pin_0, U1.PB7(XTAL2_TOSC2)
  N9: C1.1, XTAL1.pin_1, U1.PB6(XTAL1_TOSC1)
  VIN: U3.VIN, U3.EN/UVLO, C5.0, L1.pin_1, C6.1, C7.1, PWR.pin3, R11.Pin_1
  N10: U3.DA3, D2.A
  N11: U3.SW3, D2.C, L3.pin_0
  N12: U3.SW1, L2.pin_0, D1.C
  N13: U3.DA1, D1.A
  N14: U3.SW4, D3.C, L4.pin_0
  N15: U3.DA4, D3.A
  N16: U3.RUN/SS4, C10.1
  3.3V_SHTDWN: U3.RUN/SS1, Q5.D, C8.1
  5V_SHTDWN: U3.RUN/SS3, Q6.D, C9.1
  N17: U3.RT/SNYNC, R14.Pin_1
  N18: U3.FB4, C15.0, R19.Pin_0, R20.Pin_0
  N19: U3.FB1, C11.0, R15.Pin_0, R16.Pin_0
  N20: U3.FB3, C13.0, R17.Pin_0, R18.Pin_0
  PG: U3.PG, U2.13
  N21: U3.SW5, L1.pin_0
  N22: U3.SKY, C5.1
  5V_CRITICAL: L4.pin_1, C15.1, R19.Pin_1, C16.1, U2.1, C17.0, ISP2.pin6
  N23: Q5.G, R10.Pin_1, U2.2
  N24: Q6.G, R9.Pin_1, U2.3
  U2_RST: U2.4, Q3.D, ISP2.pin3
  N25: U2.12, R11.Pin_0, R12.Pin_1
  ADC6: U1.ADC6, A6.pin1
  ADC7: U1.ADC7, A7.pin1

notes:
  3.3V
  VBAT
  FIX
  TX
  RX
  GND
  VIN
  PPS
  EN
  I2C Level Shifter
  Raspberry Pi Header
  Analog Sensor & Motion Control
  AVR Programmer
  ADC Header
  Expansion Ports
  Motors
  5V
  G
  A
  Rx
  E
  Pathfinder v2
  Andy Condon ©2016
  M
  Power Supply
  Power Monitor & Control
  Need to pick values for divider.
  Need to confirm capacitance.
  Need to fully engineer and confirm voltages.
  Find Ferrite Bead.
  Need to confirm footprint and connect.

custom parts:
  LT3514: Linear Technology LT3514 Triple Step-Down Switching Regulator Three Outputs: 2A, 1A, 1A
