# Fritzing sketch navigation (saved by Fritzing 0.9.2b)
circuit board: 8.46667cm x 5.64444cm
breadboards: 1

parts:
  U1 = atmega328 [package=dip]
  XTAL1 = Crystal [frequency="16 Mhz" package=THT]
  IC1 = IC, DIP package, 20 pins [chip_label=74LVC244]
  Raspberry_Pi_2 = Raspberry Pi 2
  C4 = Ceramic Capacitor [capacitance=100nF package="100 mil [THT, multilayer]"]
  C3 = Ceramic Capacitor [capacitance=100nF package="100 mil [THT, multilayer]"]
  R1 = Resistor [tolerance=±5% resistance=10k package=THT]
  Q1 = MOSFET-NCHANNEL [package=to-92]
  R3 = Resistor [tolerance=±5% resistance=10k package=THT]
  R2 = Resistor [tolerance=±5% resistance=100k package=THT]
  C1 = Ceramic Capacitor [capacitance=22pF package="100 mil [THT, multilayer]"]
  C2 = Ceramic Capacitor [capacitance=22pF package="100 mil [THT, multilayer]"]
  Q3 = MOSFET-NCHANNEL [package=to-92]
  Q2 = MOSFET-NCHANNEL [package=to-92]
  R4 = Resistor [tolerance=±5% resistance=10k package=THT]
  R5 = Resistor [tolerance=±5% resistance=10k package=THT]
  R6 = Resistor [tolerance=±5% resistance=10k package=THT]
  R7 = Resistor [tolerance=±5% resistance=10k package=THT]
  Port4 = shrouded pin header, 6 pins [form="♂ (shrouded male)"]
  Port3 = shrouded pin header, 6 pins [form="♂ (shrouded male)"]
  Port2 = shrouded pin header, 6 pins [form="♂ (shrouded male)"]
  Port1 = shrouded pin header, 6 pins [form="♂ (shrouded male)"]
  GPS = female pin header, 9 pins [form="♀ (female)"]
  Port5 = shrouded pin header, 6 pins [form="♂ (shrouded male)"]

nets (from the schematic view):
  AVR_RST: U1.RESET, Q1.D, R3.Pin_1
  5V: U1.D4, U1.AVCC, C4.0, C3.1, R3.Pin_0, R6.Pin_1, R7.Pin_1, Port4.pin1, Port3.pin1, Port2.pin1, Port1.pin1, Port5.pin1
  GND: U1.GND, IC1.pin10, IC1.pin11, IC1.pin13, IC1.pin15, IC1.pin17, Raspberry_Pi_2.GND, C4.1, C3.0, Q1.S, R2.Pin_0, C1.1, C2.1, Port4.pin3, Port4.pin6, Port3.pin3, Port3.pin6, Port2.pin3, Port2.pin6, Port1.pin3, Port1.pin6, GPS.pin7, Port5.pin3, Port5.pin6
  N1: U1.XLAT1, XTAL1.pin_1, C2.0
  N2: U1.XLAT2, XTAL1.pin_0, C1.0
  AVR_MOSI: U1.D11_(PWM), IC1.pin14
  AVR_MISO: U1.D12, IC1.pin8
  AVR_SCK: U1.D13, IC1.pin16
  5V_SDA: U1.A4, Q2.D, R7.Pin_0, Port4.pin4, Port3.pin4, Port2.pin4, Port1.pin4, Port5.pin4
  5V_SCL: U1.A5, Q3.D, R6.Pin_0, Port4.pin5, Port3.pin5, Port2.pin5, Port1.pin5, Port5.pin5
  PI_CE0: IC1.pin1, Raspberry_Pi_2.GPIO8, R1.Pin_0
  PI_SCK: IC1.pin4, Raspberry_Pi_2.GPIO11
  PI_MOSI: IC1.pin6, Raspberry_Pi_2.GPIO10
  PI_MISO: IC1.pin12, Raspberry_Pi_2.GPIO9
  N3: IC1.pin18, Q1.G, R2.Pin_1
  3.3V: IC1.pin19, IC1.pin20, R1.Pin_1, Q3.G, Q2.G, R4.Pin_1, R5.Pin_1, Port4.pin2, Port3.pin2, Port2.pin2, Port1.pin2, GPS.pin1, Port5.pin2
  3.3V_SDA: Raspberry_Pi_2.GPIO2, Q2.S, R4.Pin_0
  3.3V_SCL: Raspberry_Pi_2.GPIO3, Q3.S, R5.Pin_0
  N4: Raspberry_Pi_2.GPIO15, GPS.pin5
  N5: Raspberry_Pi_2.GPIO14, GPS.pin6

notes:
  3.3V
  VBAT
  FIX
  TX
  RX
  GND
  VIN
  PPS
  EN
  I2C Level Shifter
  Raspberry Pi Header
  Atmel ATMEGA 328p
  ATMEGA Programmer
