# Fritzing sketch navigator (saved by Fritzing 0.9.2b)
breadboards: 1

parts:
  U1 = atmega328 [package=dip]
  XTAL1 = Crystal [frequency="16 Mhz" package=THT]
  IC1 = IC, DIP package, 20 pins [chip_label=74LVC244]
  GPS1 = female pin header, 9 pins [form="♀ (female)"]
  Raspberry_Pi_2 = Raspberry Pi 2
  Power = shrouded pin header, 6 pins [form="♂ (shrouded male)"]
  C1 = Ceramic Capacitor [capacitance=22pF package="100 mil [THT, multilayer]"]
  C2 = Ceramic Capacitor [capacitance=22pF package="100 mil [THT, multilayer]"]
  C3 = Ceramic Capacitor [capacitance=100nF package="100 mil [THT, multilayer]"]
  C4 = Ceramic Capacitor [capacitance=100nF package="100 mil [THT, multilayer]"]
  R1 = Resistor [tolerance=±5% resistance=10k package=THT]
  Q1 = MOSFET-NCHANNEL [package=to-92]  # not connected

nets:
  N1: U1.VCC, U1.AVCC, Power.pin1, C3.0, C4.1
  GND: U1.GND, IC1.pin10, IC1.pin11, IC1.pin13, IC1.pin15, IC1.pin17, GPS1.pin7, Raspberry_Pi_2.GND, Power.pin3, Power.pin6, C1.1, C2.0, C3.1, C4.0
  N2: U1.XLAT1, XTAL1.pin_1, C1.0
  N3: U1.XLAT2, XTAL1.pin_0, C2.1
  N4: IC1.pin1, Raspberry_Pi_2.GPIO8, R1.Pin_0
  N5: IC1.pin2, IC1.pin19, IC1.pin20, GPS1.pin1, Power.pin2, R1.Pin_1
  N6: IC1.pin4, Raspberry_Pi_2.GPIO11
  N7: IC1.pin6, Raspberry_Pi_2.GPIO10
  N8: IC1.pin8, Raspberry_Pi_2.GPIO9
  N9: GPS1.pin5, Raspberry_Pi_2.GPIO15
  N10: GPS1.pin6, Raspberry_Pi_2.GPIO14

notes:
  3.3V
  VBAT
  FIX
  TX
  RX
  GND
  VIN
  PPS
  EN
  BAT2 LVL
  BAT1 LVL
  5V
